# Fritzing sketch IceBreaker (saved by Fritzing 0.9.3b)

parts:
  Part4 = LilyPad Arduino Simple Board
  Part5 = LilyPad XBee
  U2 = Vibration Motor- ROB-08449 [package=vibe-motor-10mm]
  S2 = Momentary Switch [package=ksa_sealed_tac_switch]
  R2 = Resistor [tolerance=±5% resistance=10k package=THT]
  LED1 = Super Flux RGB LED (com. anode)

nets:
  N1: Part4.A5, Part5.D11
  N2: Part4.D11, U2.-
  N3: Part4.D5, LED1.blue_cathode, LED1.green_cathode
  GND: Part4.GND, Part5.GND, U2.+, R2.Pin_0, LED1.common_anode
  VCC: Part4.VCC, Part5.VCC, S2.1
  N4: S2.3, R2.Pin_1
